// Logisim project RISKY.circ as structural Verilog: 21 circuits, main circuit CPU
module CPU (
);

  wire ALU32INEN, ALU32OUTEN, ALUINEN, ALUOUTEN, CLK, CONT, CUIMMEDIATE, HALT, jmpgate_1_pcloadout,
       KBAVAILABLEIN, kbctrl_1_kbclk, kbctrl_1_kbrd, kbctrl_1_kbrst, keyboard_1_avail, PAGELOAD, PAGEOUT,
       pc_1_pcoverflow, PCLOAD, PCOUT, RAMLOAD, RAMOFFSETEN, RAMSTORE, REGINEN1, REGINEN2, REGMOV, REGOUTEN1,
       REGOUTEN2, REGOUTEN3, REGOUTEN4, RESET, SPOUT, STATEOUTEN, terminal_1_clearout, terminal_1_clkout,
       terminal_1_enout;
  wire [1:0] REGSELMODESEL, SPMODE;
  wire [2:0] RAMMODESEL;
  wire [3:0] ALUOPSEL, JMPTYPE, regsel_1_reginsel1, regsel_1_reginsel2, regsel_1_regoutsel1,
       regsel_1_regoutsel2, regsel_1_regoutsel3, regsel_1_regoutsel4;
  wire [6:0] keyboard_1_data, terminal_1_asciiout;
  wire [7:0] alu_1_alu32statusout, alu_1_alustatusout;
  wire [13:0] status_1_statusout;
  wire [15:0] alu_1_aluout, alureg_1_aluout1, alureg_1_aluout2, alureg_1_regdataout2, jmpgate_1_stateout,
       pc_1_pcout, ram_1_ramdataout, ramreg_1_pageout_2, ramreg_1_ramaddrout, ramreg_1_ramdatain,
       reg_1_regdataout1, reg_1_regdataout2, reg_1_regdataout3, reg_1_regdataout4;
  wire [31:0] alu_1_alu32out, alureg_1_alu32in1, alureg_1_alu32in2, rom_1_romout;

  STATUS status_1 (
    .STATUSIN(alu_1_alustatusout), .STATUS32IN(alu_1_alu32statusout), .ALUINEN(ALUINEN),
    .ALU32INEN(ALU32INEN), .STATUSOUT(status_1_statusout), .CLKIN(CLK), .RESET(RESET));
  JMPGATE jmpgate_1 (
    .STATUSIN(status_1_statusout), .KBAVAILABLEIN(KBAVAILABLEIN), .PCLOADIN(PCLOAD), .JMPTYPE(JMPTYPE),
    .PCLOADOUT(jmpgate_1_pcloadout), .STATEOUTEN(STATEOUTEN), .STATEOUT(jmpgate_1_stateout));
  Clock clock_1 (.out(CLK));
  PC pc_1 (
    .PCLOAD(jmpgate_1_pcloadout), .PCLOADADDR1(reg_1_regdataout1), .PCOUT(pc_1_pcout),
    .PCOVERFLOW(pc_1_pcoverflow), .RESET(RESET), .HALT(HALT), .CONT(CONT), .PCCLKIN(CLK),
    .PCLOADADDR2(jmpgate_1_stateout), .PCMOVOUT(jmpgate_1_stateout), .PCOUTEN(PCOUT));
  LED OVERFLOW (.in(pc_1_pcoverflow));
  ROM rom_1 (.ROMIN(pc_1_pcout), .ROMOUT(rom_1_romout));
  REGSEL regsel_1 (
    .REGSELINSTRIN(rom_1_romout), .REGSELMODESEL(REGSELMODESEL), .REGINSEL1(regsel_1_reginsel1),
    .REGINSEL2(regsel_1_reginsel2), .REGOUTSEL1(regsel_1_regoutsel1), .REGOUTSEL2(regsel_1_regoutsel2),
    .REGOUTSEL3(regsel_1_regoutsel3), .REGOUTSEL4(regsel_1_regoutsel4));
  ALUREG alureg_1 (
    .ALUIMMEDIATEIN(rom_1_romout), .ALUIMMEDIATEIN_2(CUIMMEDIATE), .ALUOUT1(alureg_1_aluout1),
    .ALUOUT2(alureg_1_aluout2), .ALU32IN1(alureg_1_alu32in1), .ALU32IN2(alureg_1_alu32in2),
    .ALUIN1(alu_1_aluout), .ALUIN2(alu_1_alu32out), .REGDATAOUT1(jmpgate_1_stateout),
    .REGDATAOUT2(alureg_1_regdataout2), .REGDATAIN1(reg_1_regdataout1), .REGDATAIN2(reg_1_regdataout2),
    .REGDATAIN3(reg_1_regdataout3), .REGDATAIN4(reg_1_regdataout4));
  ALU alu_1 (
    .ALUDATAIN0(alureg_1_aluout1), .ALUDATAIN1(alureg_1_aluout2), .ALU32DATAIN0(alureg_1_alu32in1),
    .ALU32DATAIN1(alureg_1_alu32in2), .ALUOPSEL(ALUOPSEL), .ALUOUTEN(ALUOUTEN), .ALUOUT(alu_1_aluout),
    .ALU32OUT(alu_1_alu32out), .ALUINEN(ALUINEN), .ALU32INEN(ALU32INEN), .ALUSTATUSOUT(alu_1_alustatusout),
    .ALU32STATUSOUT(alu_1_alu32statusout), .ALU32OUTEN(ALU32OUTEN));
  REG reg_1 (
    .RESET(RESET), .REGDATAOUT1(reg_1_regdataout1), .REGDATAOUT2(reg_1_regdataout2),
    .REGDATAOUT3(reg_1_regdataout3), .REGDATAOUT4(reg_1_regdataout4), .REGINEN2(REGINEN2),
    .REGINSEL2(regsel_1_reginsel2), .REGINEN1(REGINEN1), .REGINSEL1(regsel_1_reginsel1),
    .REGDATAIN2(alureg_1_regdataout2), .REGDATAIN1(jmpgate_1_stateout), .REGMOV(REGMOV),
    .REGOUTSEL1(regsel_1_regoutsel1), .REGOUTEN1(REGOUTEN1), .REGOUTSEL2(regsel_1_regoutsel2),
    .REGOUTEN2(REGOUTEN2), .REGOUTSEL3(regsel_1_regoutsel3), .REGOUTEN3(REGOUTEN3),
    .REGOUTSEL4(regsel_1_regoutsel4), .REGOUTEN4(REGOUTEN4), .REGCLKIN(CLK));
  RAMREG ramreg_1 (
    .REGDATAOUT1(jmpgate_1_stateout), .REGDATAOUT2(alureg_1_regdataout2), .REGDATAIN1(reg_1_regdataout1),
    .REGDATAIN2(reg_1_regdataout2), .REGDATAIN3(reg_1_regdataout3), .REGDATAIN4(reg_1_regdataout4),
    .RAMDATAIN(ramreg_1_ramdatain), .RAMADDROUT(ramreg_1_ramaddrout), .RAMDATAOUT(ram_1_ramdataout),
    .RAMMODESEL(RAMMODESEL), .RAMIMMEDIATEIN(rom_1_romout), .SPMODE(SPMODE), .CLKIN(CLK), .RESET(RESET),
    .PAGEOUT(PAGEOUT), .PAGELOAD(PAGELOAD), .PAGEOUT_2(ramreg_1_pageout_2), .RAMOFFSETEN(RAMOFFSETEN),
    .SPOUT(SPOUT));
  RAM ram_1 (
    .RAMADDRIN(ramreg_1_ramaddrout), .RAMDATAIN(ramreg_1_ramdatain), .RAMPAGEIN(ramreg_1_pageout_2),
    .RAMDATAOUT(ram_1_ramdataout), .RESET(RESET), .RAMLOAD(RAMLOAD), .RAMSTORE(RAMSTORE), .RAMCLKIN(CLK));
  TTY #(.rows(24), .cols(80)) tty_1 (
    .data(terminal_1_asciiout), .clk(terminal_1_clkout), .we(terminal_1_enout), .clr(terminal_1_clearout));
  TERMINAL terminal_1 (
    .RAMADDRIN(ramreg_1_ramaddrout), .RAMDATAIN(ramreg_1_ramdatain), .RAMPAGEIN(ramreg_1_pageout_2),
    .ASCIIOUT(terminal_1_asciiout), .CLKOUT(terminal_1_clkout), .RAMDATAOUT(ram_1_ramdataout), .RESET(RESET),
    .RAMLOAD(RAMLOAD), .RAMSTORE(RAMSTORE), .RAMCLKIN(CLK), .ENOUT(terminal_1_enout),
    .CLEAROUT(terminal_1_clearout));
  DATA data_1 (
    .RAMADDRIN(ramreg_1_ramaddrout), .RAMPAGEIN(ramreg_1_pageout_2), .RAMDATAOUT(ram_1_ramdataout),
    .RAMLOAD(RAMLOAD));
  CU cu_1 (
    .CUROMIN(rom_1_romout), .REGINEN1(REGINEN1), .REGINEN2(REGINEN2), .REGOUTEN1(REGOUTEN1),
    .REGOUTEN2(REGOUTEN2), .REGOUTEN3(REGOUTEN3), .REGOUTEN4(REGOUTEN4), .REGMOV(REGMOV), .ALUINEN(ALUINEN),
    .ALU32INEN(ALU32INEN), .ALUOUTEN(ALUOUTEN), .ALUOPSEL(ALUOPSEL), .CUIMMEDIATE(CUIMMEDIATE),
    .REGSELMODESEL(REGSELMODESEL), .ALU32OUTEN(ALU32OUTEN), .RAMLOAD(RAMLOAD), .RAMSTORE(RAMSTORE),
    .RAMMODESEL(RAMMODESEL), .PCLOAD(PCLOAD), .JMPTYPE(JMPTYPE), .PCOUT(PCOUT), .SPMODE(SPMODE),
    .RESET(RESET), .PAGEOUT(PAGEOUT), .PAGELOAD(PAGELOAD), .RAMOFFSETEN(RAMOFFSETEN), .SPOUT(SPOUT),
    .STATEOUTEN(STATEOUTEN), .CUIMMEDIATEOUT(jmpgate_1_stateout));  // open: out_29
  Keyboard keyboard_1 (
    .clk(kbctrl_1_kbclk), .re(kbctrl_1_kbrd), .clr(kbctrl_1_kbrst), .avail(keyboard_1_avail),
    .data(keyboard_1_data));
  KBCTRL kbctrl_1 (
    .RAMPAGEIN(ramreg_1_pageout_2), .KBCLK(kbctrl_1_kbclk), .KBAVAILABLE(KBAVAILABLEIN),
    .RAMDATAOUT(ram_1_ramdataout), .RESET(RESET), .RAMLOAD(RAMLOAD), .RAMCLKIN(CLK), .KBRD(kbctrl_1_kbrd),
    .KBRST(kbctrl_1_kbrst), .KBAV(keyboard_1_avail), .KBDAT(keyboard_1_data));
endmodule

module REG (
  input  REGMOV,
  input  REGINEN2,
  input  [3:0] REGINSEL2,
  input  REGINEN1,
  input  [3:0] REGINSEL1,
  input  [15:0] REGDATAIN2,
  input  [15:0] REGDATAIN1,
  input  [3:0] REGOUTSEL1,
  input  REGOUTEN1,
  input  [3:0] REGOUTSEL2,
  input  REGOUTEN2,
  input  [3:0] REGOUTSEL3,
  input  REGOUTEN3,
  input  [3:0] REGOUTSEL4,
  input  REGOUTEN4,
  input  RESET,
  input  REGCLKIN,
  output [15:0] REGDATAOUT1,
  output [15:0] REGDATAOUT2,
  output [15:0] REGDATAOUT3,
  output [15:0] REGDATAOUT4
);

  wire decoder_1_out0, decoder_1_out1, decoder_1_out2, decoder_1_out3, decoder_1_out4, decoder_1_out5,
       decoder_1_out6, decoder_1_out7, decoder_1_out8, decoder_1_out9, decoder_1_out10, decoder_1_out11,
       decoder_1_out12, decoder_1_out13, decoder_1_out14, decoder_1_out15, decoder_2_out0, decoder_2_out1,
       decoder_2_out2, decoder_2_out3, decoder_2_out4, decoder_2_out5, decoder_2_out6, decoder_2_out7,
       decoder_2_out8, decoder_2_out9, decoder_2_out10, decoder_2_out11, decoder_2_out12, decoder_2_out13,
       decoder_2_out14, decoder_2_out15, n16xor_1_out_33, n16xor_1_out_34, n16xor_1_out_35, n16xor_1_out_36,
       n16xor_1_out_37, n16xor_1_out_38, n16xor_1_out_39, n16xor_1_out_40, n16xor_1_out_41, n16xor_1_out_42,
       n16xor_1_out_43, n16xor_1_out_44, n16xor_1_out_45, n16xor_1_out_46, n16xor_1_out_47, n16xor_1_out_48;
  wire [15:0] multiplexer_1_out, multiplexer_2_out, R0_q, R1_q, R2_q, R3_q, R4_q, R5_q, R6_q, R7_q, R8_q,
       R9_q, R10_q, R11_q, R12_q, R13_q, R14_q, R15_q, regdataindemux_1_r0, regdataindemux_1_r1,
       regdataindemux_1_r2, regdataindemux_1_r3, regdataindemux_1_r4, regdataindemux_1_r5,
       regdataindemux_1_r6, regdataindemux_1_r7, regdataindemux_1_r8, regdataindemux_1_r9,
       regdataindemux_1_r10, regdataindemux_1_r11, regdataindemux_1_r12, regdataindemux_1_r13,
       regdataindemux_1_r14, regdataindemux_1_r15;

  Decoder #(.select(4), .disabled(0)) decoder_1 (
    .out0(decoder_1_out0), .out1(decoder_1_out1), .out2(decoder_1_out2), .out3(decoder_1_out3),
    .out4(decoder_1_out4), .out5(decoder_1_out5), .out6(decoder_1_out6), .out7(decoder_1_out7),
    .out8(decoder_1_out8), .out9(decoder_1_out9), .out10(decoder_1_out10), .out11(decoder_1_out11),
    .out12(decoder_1_out12), .out13(decoder_1_out13), .out14(decoder_1_out14), .out15(decoder_1_out15),
    .sel(REGINSEL1), .en(REGINEN1));
  Decoder #(.select(4), .disabled(0)) decoder_2 (
    .out0(decoder_2_out0), .out1(decoder_2_out1), .out2(decoder_2_out2), .out3(decoder_2_out3),
    .out4(decoder_2_out4), .out5(decoder_2_out5), .out6(decoder_2_out6), .out7(decoder_2_out7),
    .out8(decoder_2_out8), .out9(decoder_2_out9), .out10(decoder_2_out10), .out11(decoder_2_out11),
    .out12(decoder_2_out12), .out13(decoder_2_out13), .out14(decoder_2_out14), .out15(decoder_2_out15),
    .sel(REGINSEL2), .en(REGINEN2));
  Multiplexer #(.width(16), .disabled(0), .enable("false")) multiplexer_1 (
    .in0(REGDATAIN2), .in1(REGDATAOUT4), .out(multiplexer_1_out), .sel(REGMOV));
  REGDATAINDEMUX regdataindemux_1 (
    .in_1(REGINEN1), .in_4(REGINSEL1), .in_5(REGINEN2), .in_6(REGINSEL2), .in_2(multiplexer_1_out),
    .in_3(multiplexer_2_out), .R3(regdataindemux_1_r3), .R2(regdataindemux_1_r2), .R1(regdataindemux_1_r1),
    .R0(regdataindemux_1_r0), .R7(regdataindemux_1_r7), .R6(regdataindemux_1_r6), .R5(regdataindemux_1_r5),
    .R4(regdataindemux_1_r4), .R11(regdataindemux_1_r11), .R10(regdataindemux_1_r10),
    .R9(regdataindemux_1_r9), .R8(regdataindemux_1_r8), .R15(regdataindemux_1_r15),
    .R14(regdataindemux_1_r14), .R13(regdataindemux_1_r13), .R12(regdataindemux_1_r12));
  _16xOR u_16xor_1 (
    .in_1(decoder_1_out0), .in_2(decoder_1_out1), .in_3(decoder_1_out2), .in_4(decoder_1_out3),
    .in_5(decoder_1_out4), .in_6(decoder_1_out5), .in_7(decoder_1_out6), .in_8(decoder_1_out7),
    .in_9(decoder_1_out8), .in_10(decoder_1_out9), .in_11(decoder_1_out10), .in_12(decoder_1_out11),
    .in_13(decoder_1_out12), .in_14(decoder_1_out13), .in_15(decoder_1_out14), .in_16(decoder_1_out15),
    .in_17(decoder_2_out0), .in_18(decoder_2_out1), .in_19(decoder_2_out2), .in_20(decoder_2_out3),
    .in_21(decoder_2_out4), .in_22(decoder_2_out5), .in_23(decoder_2_out6), .in_24(decoder_2_out7),
    .in_25(decoder_2_out8), .in_26(decoder_2_out9), .in_27(decoder_2_out10), .in_28(decoder_2_out11),
    .in_29(decoder_2_out12), .in_30(decoder_2_out13), .in_31(decoder_2_out14), .in_32(decoder_2_out15),
    .out_33(n16xor_1_out_33), .out_34(n16xor_1_out_34), .out_35(n16xor_1_out_35), .out_36(n16xor_1_out_36),
    .out_37(n16xor_1_out_37), .out_38(n16xor_1_out_38), .out_39(n16xor_1_out_39), .out_40(n16xor_1_out_40),
    .out_41(n16xor_1_out_41), .out_42(n16xor_1_out_42), .out_43(n16xor_1_out_43), .out_44(n16xor_1_out_44),
    .out_45(n16xor_1_out_45), .out_46(n16xor_1_out_46), .out_47(n16xor_1_out_47), .out_48(n16xor_1_out_48));
  Multiplexer #(.width(16), .disabled(0), .enable("false")) multiplexer_2 (
    .in0(REGDATAIN1), .in1(REGDATAOUT3), .out(multiplexer_2_out), .sel(REGMOV));
  Register #(.width(16)) R0 (.D(regdataindemux_1_r0), .en(n16xor_1_out_33), .Q(R0_q), .clk(REGCLKIN), .clr(RESET));
  Register #(.width(16)) R4 (.D(regdataindemux_1_r4), .en(n16xor_1_out_37), .Q(R4_q), .clk(REGCLKIN), .clr(RESET));
  Register #(.width(16)) R8 (.D(regdataindemux_1_r8), .en(n16xor_1_out_41), .Q(R8_q), .clk(REGCLKIN), .clr(RESET));
  Register #(.width(16)) R12 (.D(regdataindemux_1_r12), .en(n16xor_1_out_45), .Q(R12_q), .clk(REGCLKIN), .clr(RESET));
  Register #(.width(16)) R1 (.D(regdataindemux_1_r1), .en(n16xor_1_out_34), .Q(R1_q), .clk(REGCLKIN), .clr(RESET));
  Register #(.width(16)) R5 (.D(regdataindemux_1_r5), .en(n16xor_1_out_38), .Q(R5_q), .clk(REGCLKIN), .clr(RESET));
  Register #(.width(16)) R9 (.D(regdataindemux_1_r9), .en(n16xor_1_out_42), .Q(R9_q), .clk(REGCLKIN), .clr(RESET));
  Register #(.width(16)) R13 (.D(regdataindemux_1_r13), .en(n16xor_1_out_46), .Q(R13_q), .clk(REGCLKIN), .clr(RESET));
  Register #(.width(16)) R2 (.D(regdataindemux_1_r2), .en(n16xor_1_out_35), .Q(R2_q), .clk(REGCLKIN), .clr(RESET));
  Register #(.width(16)) R6 (.D(regdataindemux_1_r6), .en(n16xor_1_out_39), .Q(R6_q), .clk(REGCLKIN), .clr(RESET));
  Register #(.width(16)) R10 (.D(regdataindemux_1_r10), .en(n16xor_1_out_43), .Q(R10_q), .clk(REGCLKIN), .clr(RESET));
  Register #(.width(16)) R14 (.D(regdataindemux_1_r14), .en(n16xor_1_out_47), .Q(R14_q), .clk(REGCLKIN), .clr(RESET));
  Register #(.width(16)) R3 (.D(regdataindemux_1_r3), .en(n16xor_1_out_36), .Q(R3_q), .clk(REGCLKIN), .clr(RESET));
  Register #(.width(16)) R7 (.D(regdataindemux_1_r7), .en(n16xor_1_out_40), .Q(R7_q), .clk(REGCLKIN));  // open: clr
  Register #(.width(16)) R11 (.D(regdataindemux_1_r11), .en(n16xor_1_out_44), .Q(R11_q), .clk(REGCLKIN), .clr(RESET));
  Register #(.width(16)) R15 (.D(regdataindemux_1_r15), .en(n16xor_1_out_48), .Q(R15_q), .clk(REGCLKIN), .clr(RESET));
  Multiplexer #(.select(4), .width(16)) multiplexer_3 (
    .in0(R0_q), .in1(R1_q), .in2(R2_q), .in3(R3_q), .in4(R4_q), .in5(R5_q), .in6(R6_q), .in7(R7_q),
    .in8(R8_q), .in9(R9_q), .in10(R10_q), .in11(R11_q), .in12(R12_q), .in13(R13_q), .in14(R14_q),
    .in15(R15_q), .out(REGDATAOUT1), .sel(REGOUTSEL1), .en(REGOUTEN1));
  Multiplexer #(.select(4), .width(16)) multiplexer_4 (
    .in0(R0_q), .in1(R1_q), .in2(R2_q), .in3(R3_q), .in4(R4_q), .in5(R5_q), .in6(R6_q), .in7(R7_q),
    .in8(R8_q), .in9(R9_q), .in10(R10_q), .in11(R11_q), .in12(R12_q), .in13(R13_q), .in14(R14_q),
    .in15(R15_q), .out(REGDATAOUT2), .sel(REGOUTSEL2), .en(REGOUTEN2));
  Multiplexer #(.select(4), .width(16)) multiplexer_5 (
    .in0(R0_q), .in1(R1_q), .in2(R2_q), .in3(R3_q), .in4(R4_q), .in5(R5_q), .in6(R6_q), .in7(R7_q),
    .in8(R8_q), .in9(R9_q), .in10(R10_q), .in11(R11_q), .in12(R12_q), .in13(R13_q), .in14(R14_q),
    .in15(R15_q), .out(REGDATAOUT3), .sel(REGOUTSEL3), .en(REGOUTEN3));
  Multiplexer #(.select(4), .width(16)) multiplexer_6 (
    .in0(R0_q), .in1(R1_q), .in2(R2_q), .in3(R3_q), .in4(R4_q), .in5(R5_q), .in6(R6_q), .in7(R7_q),
    .in8(R8_q), .in9(R9_q), .in10(R10_q), .in11(R11_q), .in12(R12_q), .in13(R13_q), .in14(R14_q),
    .in15(R15_q), .out(REGDATAOUT4), .sel(REGOUTSEL4), .en(REGOUTEN4));
endmodule

module ALU (
  input  ALUINEN,
  input  [15:0] ALUDATAIN0,
  input  [15:0] ALUDATAIN1,
  input  [3:0] ALUOPSEL,
  input  ALUOUTEN,
  input  ALU32INEN,
  input  [31:0] ALU32DATAIN0,
  input  [31:0] ALU32DATAIN1,
  input  ALU32OUTEN,
  output [15:0] ALUOUT,
  output [7:0] ALUSTATUSOUT,
  output [31:0] ALU32OUT,
  output [7:0] ALU32STATUSOUT
);

  wire [3:0] bit_extender_1_out, bit_extender_2_out;
  wire [4:0] bit_extender_3_out, bit_extender_4_out;
  wire [15:0] adder_1_out, and_1_out, controlled_buffer_1_out, controlled_buffer_2_out, divider_1_out,
       divider_1_rem, multiplier_1_cout, multiplier_1_out, negator_1_out, not_1_out, or_1_out, shifter_1_out,
       shifter_2_out, subtractor_1_out, xor_1_out;
  wire [31:0] adder_2_out, and_2_out, controlled_buffer_3_out, controlled_buffer_4_out, divider_2_out,
       divider_2_rem, multiplier_2_cout, multiplier_2_out, negator_2_out, not_2_out, or_2_out, shifter_3_out,
       shifter_4_out, subtractor_2_out, xor_2_out;

  assign controlled_buffer_1_out = ALUINEN ? ALUDATAIN0 : 16'bz;  // Controlled_Buffer controlled_buffer_1
  assign controlled_buffer_2_out = ALUINEN ? ALUDATAIN1 : 16'bz;  // Controlled_Buffer controlled_buffer_2
  assign controlled_buffer_3_out = ALU32INEN ? ALU32DATAIN0 : 32'bz;  // Controlled_Buffer controlled_buffer_3
  assign controlled_buffer_4_out = ALU32INEN ? ALU32DATAIN1 : 32'bz;  // Controlled_Buffer controlled_buffer_4
  Bit_Extender #(.in_width(16), .out_width(4)) bit_extender_1 (.in(controlled_buffer_2_out), .out(bit_extender_1_out));
  Bit_Extender #(.in_width(16), .out_width(4)) bit_extender_2 (.in(controlled_buffer_2_out), .out(bit_extender_2_out));
  Bit_Extender #(.in_width(32), .out_width(5)) bit_extender_3 (.in(controlled_buffer_4_out), .out(bit_extender_3_out));
  Bit_Extender #(.in_width(32), .out_width(5)) bit_extender_4 (.in(controlled_buffer_4_out), .out(bit_extender_4_out));
  Adder #(.width(16)) adder_1 (
    .a(controlled_buffer_1_out), .b(controlled_buffer_2_out), .out(adder_1_out), .cout(ALUSTATUSOUT[0]));  // open: cin
  Subtractor #(.width(16)) subtractor_1 (
    .a(controlled_buffer_1_out), .b(controlled_buffer_2_out), .out(subtractor_1_out), .bout(ALUSTATUSOUT[1]));  // open: bin
  Multiplier #(.width(16)) multiplier_1 (
    .a(controlled_buffer_1_out), .b(controlled_buffer_2_out), .out(multiplier_1_out), .cout(multiplier_1_cout));  // open: cin
  Divider #(.width(16)) divider_1 (
    .a(controlled_buffer_1_out), .b(controlled_buffer_2_out), .out(divider_1_out), .rem(divider_1_rem));  // open: upper
  Negator #(.width(16)) negator_1 (.in(controlled_buffer_2_out), .out(negator_1_out));
  Comparator #(.width(16)) comparator_1 (
    .a(controlled_buffer_1_out), .b(controlled_buffer_2_out), .gt(ALUSTATUSOUT[4]), .eq(ALUSTATUSOUT[5]),
    .lt(ALUSTATUSOUT[6]));
  Shifter #(.width(16)) shifter_1 (.in(controlled_buffer_1_out), .\dist (bit_extender_1_out), .out(shifter_1_out));
  Shifter #(.width(16), .shift("lr")) shifter_2 (
    .in(controlled_buffer_1_out), .\dist (bit_extender_2_out), .out(shifter_2_out));
  assign and_1_out = controlled_buffer_1_out & controlled_buffer_2_out;  // AND_Gate and_1, 16 bits wide
  assign or_1_out = controlled_buffer_1_out | controlled_buffer_2_out;  // OR_Gate or_1, 16 bits wide
  assign xor_1_out = controlled_buffer_1_out ^ controlled_buffer_2_out;  // XOR_Gate xor_1, 16 bits wide
  assign not_1_out = ~controlled_buffer_2_out;  // NOT_Gate not_1, 16 bits wide
  Adder #(.width(32)) adder_2 (
    .a(controlled_buffer_3_out), .b(controlled_buffer_4_out), .out(adder_2_out), .cout(ALU32STATUSOUT[0]));  // open: cin
  Subtractor #(.width(32)) subtractor_2 (
    .a(controlled_buffer_3_out), .b(controlled_buffer_4_out), .out(subtractor_2_out), .bout(ALU32STATUSOUT[1]));  // open: bin
  Multiplier #(.width(32)) multiplier_2 (
    .a(controlled_buffer_3_out), .b(controlled_buffer_4_out), .out(multiplier_2_out), .cout(multiplier_2_cout));  // open: cin
  Divider #(.width(32)) divider_2 (
    .a(controlled_buffer_3_out), .b(controlled_buffer_4_out), .out(divider_2_out), .rem(divider_2_rem));  // open: upper
  Negator #(.width(32)) negator_2 (.in(controlled_buffer_4_out), .out(negator_2_out));
  Comparator #(.width(32)) comparator_2 (
    .a(controlled_buffer_3_out), .b(controlled_buffer_4_out), .gt(ALU32STATUSOUT[4]), .eq(ALU32STATUSOUT[5]),
    .lt(ALU32STATUSOUT[6]));
  Shifter #(.width(32)) shifter_3 (.in(controlled_buffer_3_out), .\dist (bit_extender_3_out), .out(shifter_3_out));
  Shifter #(.width(32), .shift("lr")) shifter_4 (
    .in(controlled_buffer_3_out), .\dist (bit_extender_4_out), .out(shifter_4_out));
  assign and_2_out = controlled_buffer_3_out & controlled_buffer_4_out;  // AND_Gate and_2, 32 bits wide
  assign or_2_out = controlled_buffer_3_out | controlled_buffer_4_out;  // OR_Gate or_2, 32 bits wide
  assign xor_2_out = controlled_buffer_3_out ^ controlled_buffer_4_out;  // XOR_Gate xor_2, 32 bits wide
  assign not_2_out = ~controlled_buffer_4_out;  // NOT_Gate not_2, 32 bits wide
  Multiplexer #(.select(4), .width(16)) multiplexer_1 (
    .in0(adder_1_out), .in1(subtractor_1_out), .in2(multiplier_1_out), .in3(multiplier_1_cout),
    .in4(divider_1_out), .in5(divider_1_rem), .in6(negator_1_out), .in7(shifter_1_out), .in8(shifter_2_out),
    .in9(and_1_out), .in10(or_1_out), .in11(xor_1_out), .in12(not_1_out), .out(ALUOUT), .sel(ALUOPSEL),
    .en(ALUOUTEN));  // open: in13, in14, in15
  Multiplexer #(.select(4), .width(32)) multiplexer_2 (
    .in0(adder_2_out), .in1(subtractor_2_out), .in2(multiplier_2_out), .in3(multiplier_2_cout),
    .in4(divider_2_out), .in5(divider_2_rem), .in6(negator_2_out), .in7(shifter_3_out), .in8(shifter_4_out),
    .in9(and_2_out), .in10(or_2_out), .in11(xor_2_out), .in12(not_2_out), .out(ALU32OUT), .sel(ALUOPSEL),
    .en(ALU32OUTEN));  // open: in13, in14, in15
  Comparator #(.width(16)) comparator_3 (.a(ALUOUT), .b({16{1'b0}}), .eq(ALUSTATUSOUT[3]));  // open: gt, lt
  Comparator #(.width(32)) comparator_4 (.a(ALU32OUT), .b({32{1'b0}}), .eq(ALU32STATUSOUT[3]));  // open: gt, lt

  assign ALU32STATUSOUT[2] = ALU32OUT[31];
  assign ALUSTATUSOUT[2] = ALUOUT[15];
endmodule

module _16xOR (
  input  in_1,
  input  in_2,
  input  in_3,
  input  in_4,
  input  in_5,
  input  in_6,
  input  in_7,
  input  in_8,
  input  in_9,
  input  in_10,
  input  in_11,
  input  in_12,
  input  in_13,
  input  in_14,
  input  in_15,
  input  in_16,
  input  in_17,
  input  in_18,
  input  in_19,
  input  in_20,
  input  in_21,
  input  in_22,
  input  in_23,
  input  in_24,
  input  in_25,
  input  in_26,
  input  in_27,
  input  in_28,
  input  in_29,
  input  in_30,
  input  in_31,
  input  in_32,
  output out_33,
  output out_34,
  output out_35,
  output out_36,
  output out_37,
  output out_38,
  output out_39,
  output out_40,
  output out_41,
  output out_42,
  output out_43,
  output out_44,
  output out_45,
  output out_46,
  output out_47,
  output out_48
);

  or or_1 (out_33, in_1, in_17);
  or or_2 (out_34, in_2, in_18);
  or or_3 (out_35, in_3, in_19);
  or or_4 (out_36, in_4, in_20);
  or or_5 (out_37, in_5, in_21);
  or or_6 (out_38, in_6, in_22);
  or or_7 (out_39, in_7, in_23);
  or or_8 (out_40, in_8, in_24);
  or or_9 (out_41, in_9, in_25);
  or or_10 (out_42, in_10, in_26);
  or or_11 (out_43, in_11, in_27);
  or or_12 (out_44, in_12, in_28);
  or or_13 (out_45, in_13, in_29);
  or or_14 (out_46, in_14, in_30);
  or or_15 (out_47, in_15, in_31);
  or or_16 (out_48, in_16, in_32);
endmodule

module REGDATAINDEMUX (
  input  in_1,
  input  [15:0] in_2,
  input  [15:0] in_3,
  input  [3:0] in_4,
  input  in_5,
  input  [3:0] in_6,
  output [15:0] R3,
  output [15:0] R2,
  output [15:0] R1,
  output [15:0] R0,
  output [15:0] R7,
  output [15:0] R6,
  output [15:0] R5,
  output [15:0] R4,
  output [15:0] R11,
  output [15:0] R10,
  output [15:0] R9,
  output [15:0] R8,
  output [15:0] R15,
  output [15:0] R14,
  output [15:0] R13,
  output [15:0] R12
);

  wire [15:0] demultiplexer_1_out0, demultiplexer_1_out1, demultiplexer_1_out2, demultiplexer_1_out3,
       demultiplexer_1_out4, demultiplexer_1_out5, demultiplexer_1_out6, demultiplexer_1_out7,
       demultiplexer_1_out8, demultiplexer_1_out9, demultiplexer_1_out10, demultiplexer_1_out11,
       demultiplexer_1_out12, demultiplexer_1_out13, demultiplexer_1_out14, demultiplexer_1_out15,
       demultiplexer_2_out0, demultiplexer_2_out1, demultiplexer_2_out2, demultiplexer_2_out3,
       demultiplexer_2_out4, demultiplexer_2_out5, demultiplexer_2_out6, demultiplexer_2_out7,
       demultiplexer_2_out8, demultiplexer_2_out9, demultiplexer_2_out10, demultiplexer_2_out11,
       demultiplexer_2_out12, demultiplexer_2_out13, demultiplexer_2_out14, demultiplexer_2_out15;

  Demultiplexer #(.select(4), .width(16), .disabled(0)) demultiplexer_1 (
    .out0(demultiplexer_1_out0), .out1(demultiplexer_1_out1), .out2(demultiplexer_1_out2),
    .out3(demultiplexer_1_out3), .out4(demultiplexer_1_out4), .out5(demultiplexer_1_out5),
    .out6(demultiplexer_1_out6), .out7(demultiplexer_1_out7), .out8(demultiplexer_1_out8),
    .out9(demultiplexer_1_out9), .out10(demultiplexer_1_out10), .out11(demultiplexer_1_out11),
    .out12(demultiplexer_1_out12), .out13(demultiplexer_1_out13), .out14(demultiplexer_1_out14),
    .out15(demultiplexer_1_out15), .in(in_2), .sel(in_6), .en(in_5));
  Demultiplexer #(.select(4), .width(16), .disabled(0)) demultiplexer_2 (
    .out0(demultiplexer_2_out0), .out1(demultiplexer_2_out1), .out2(demultiplexer_2_out2),
    .out3(demultiplexer_2_out3), .out4(demultiplexer_2_out4), .out5(demultiplexer_2_out5),
    .out6(demultiplexer_2_out6), .out7(demultiplexer_2_out7), .out8(demultiplexer_2_out8),
    .out9(demultiplexer_2_out9), .out10(demultiplexer_2_out10), .out11(demultiplexer_2_out11),
    .out12(demultiplexer_2_out12), .out13(demultiplexer_2_out13), .out14(demultiplexer_2_out14),
    .out15(demultiplexer_2_out15), .in(in_3), .sel(in_4), .en(in_1));
  assign R3 = demultiplexer_2_out3 | demultiplexer_1_out3;  // OR_Gate or_1, 16 bits wide
  assign R2 = demultiplexer_2_out2 | demultiplexer_1_out2;  // OR_Gate or_2, 16 bits wide
  assign R1 = demultiplexer_2_out1 | demultiplexer_1_out1;  // OR_Gate or_3, 16 bits wide
  assign R0 = demultiplexer_2_out0 | demultiplexer_1_out0;  // OR_Gate or_4, 16 bits wide
  assign R7 = demultiplexer_2_out7 | demultiplexer_1_out7;  // OR_Gate or_5, 16 bits wide
  assign R6 = demultiplexer_2_out6 | demultiplexer_1_out6;  // OR_Gate or_6, 16 bits wide
  assign R5 = demultiplexer_2_out5 | demultiplexer_1_out5;  // OR_Gate or_7, 16 bits wide
  assign R4 = demultiplexer_2_out4 | demultiplexer_1_out4;  // OR_Gate or_8, 16 bits wide
  assign R11 = demultiplexer_2_out11 | demultiplexer_1_out11;  // OR_Gate or_9, 16 bits wide
  assign R10 = demultiplexer_2_out10 | demultiplexer_1_out10;  // OR_Gate or_10, 16 bits wide
  assign R9 = demultiplexer_2_out9 | demultiplexer_1_out9;  // OR_Gate or_11, 16 bits wide
  assign R8 = demultiplexer_2_out8 | demultiplexer_1_out8;  // OR_Gate or_12, 16 bits wide
  assign R15 = demultiplexer_2_out15 | demultiplexer_1_out15;  // OR_Gate or_13, 16 bits wide
  assign R14 = demultiplexer_2_out14 | demultiplexer_1_out14;  // OR_Gate or_14, 16 bits wide
  assign R13 = demultiplexer_2_out13 | demultiplexer_1_out13;  // OR_Gate or_15, 16 bits wide
  assign R12 = demultiplexer_2_out12 | demultiplexer_1_out12;  // OR_Gate or_16, 16 bits wide
endmodule

module JMP (
  input  CARRY,
  input  BORROW,
  input  GT,
  input  EQ,
  input  LT,
  input  [3:0] OPIN,
  input  CLK,
  input  [3:0] JMPIN,
  input  RESET,
  output JMP
);

  wire and_1_out, comparator_1_eq, comparator_2_eq, comparator_3_gt, comparator_4_lt,
       controlled_buffer_1_out, controlled_buffer_2_out, controlled_buffer_3_out, controlled_buffer_4_out,
       controlled_buffer_5_out, decoder_1_out1, decoder_1_out2, decoder_1_out3, decoder_1_out4,
       decoder_1_out5, decoder_1_out6, decoder_1_out7, decoder_1_out8, decoder_1_out9, decoder_1_out10,
       decoder_1_out11, not_1_out, not_2_out, not_3_out, not_4_out, not_5_out, or_1_out, or_2_out, or_3_out,
       or_4_out, or_5_out, or_6_out, register_1_q, register_2_q, register_3_q, register_4_q, register_5_q;
  wire [4:0] and_2_out, pull_resistor_6_node;

  Comparator #(.width(4), .mode("unsigned")) comparator_1 (
    .a(OPIN), .b(4'b0011), .eq(comparator_1_eq));  // open: gt, lt
  Comparator #(.width(4), .mode("unsigned")) comparator_2 (
    .a(OPIN), .b(4'b0100), .eq(comparator_2_eq));  // open: gt, lt
  Comparator #(.width(4), .mode("unsigned")) comparator_3 (
    .a(OPIN), .b(4'b0111), .gt(comparator_3_gt));  // open: eq, lt
  Comparator #(.width(4), .mode("unsigned")) comparator_4 (
    .a(OPIN), .b(4'b1101), .lt(comparator_4_lt));  // open: gt, eq
  and and_1 (and_1_out, comparator_3_gt, comparator_4_lt);
  Register #(.width(1), .trigger("falling")) register_1 (
    .D(CARRY), .en(comparator_1_eq), .Q(register_1_q), .clk(CLK), .clr(RESET));
  Register #(.width(1), .trigger("falling")) register_2 (
    .D(BORROW), .en(comparator_2_eq), .Q(register_2_q), .clk(CLK), .clr(RESET));
  Register #(.width(1), .trigger("falling")) register_3 (
    .D(GT), .en(and_1_out), .Q(register_3_q), .clk(CLK), .clr(RESET));
  Register #(.width(1), .trigger("falling")) register_4 (
    .D(EQ), .en(and_1_out), .Q(register_4_q), .clk(CLK), .clr(RESET));
  Register #(.width(1), .trigger("falling")) register_5 (
    .D(LT), .en(and_1_out), .Q(register_5_q), .clk(CLK), .clr(RESET));
  Decoder #(.select(4), .disabled(0), .enable("false")) decoder_1 (
    .out1(decoder_1_out1), .out2(decoder_1_out2), .out3(decoder_1_out3), .out4(decoder_1_out4),
    .out5(decoder_1_out5), .out6(decoder_1_out6), .out7(decoder_1_out7), .out8(decoder_1_out8),
    .out9(decoder_1_out9), .out10(decoder_1_out10), .out11(decoder_1_out11), .sel(JMPIN));  // open: out0, out12, out13, out14, out15
  or or_1 (or_1_out, decoder_1_out5, decoder_1_out10);
  or or_2 (or_2_out, decoder_1_out6, decoder_1_out11);
  or or_3 (or_3_out, decoder_1_out4, decoder_1_out9);
  or or_4 (or_4_out, decoder_1_out3, decoder_1_out8);
  and and_2 (and_2_out[0], register_5_q, or_5_out);
  or or_5 (or_5_out, decoder_1_out2, decoder_1_out7);
  or or_6 (or_6_out, decoder_1_out7, decoder_1_out8, decoder_1_out9, decoder_1_out10, decoder_1_out11);
  and and_3 (and_2_out[3], register_1_q, or_1_out);
  and and_4 (and_2_out[4], register_2_q, or_2_out);
  and and_5 (and_2_out[2], register_3_q, or_3_out);
  and and_6 (and_2_out[1], register_4_q, or_4_out);
  not not_1 (not_1_out, and_2_out[0]);
  assign controlled_buffer_1_out = decoder_1_out7 ? not_1_out : 1'bz;  // Controlled_Buffer controlled_buffer_1
  assign controlled_buffer_2_out = decoder_1_out8 ? not_2_out : 1'bz;  // Controlled_Buffer controlled_buffer_2
  not not_2 (not_2_out, and_2_out[1]);
  assign controlled_buffer_3_out = decoder_1_out9 ? not_3_out : 1'bz;  // Controlled_Buffer controlled_buffer_3
  not not_3 (not_3_out, and_2_out[2]);
  assign controlled_buffer_4_out = decoder_1_out10 ? not_4_out : 1'bz;  // Controlled_Buffer controlled_buffer_4
  not not_4 (not_4_out, and_2_out[3]);
  assign controlled_buffer_5_out = decoder_1_out11 ? not_5_out : 1'bz;  // Controlled_Buffer controlled_buffer_5
  not not_5 (not_5_out, and_2_out[4]);
  Pull_Resistor pull_resistor_1 (.node(controlled_buffer_1_out));
  Pull_Resistor pull_resistor_2 (.node(controlled_buffer_2_out));
  Pull_Resistor pull_resistor_3 (.node(controlled_buffer_3_out));
  Pull_Resistor pull_resistor_4 (.node(controlled_buffer_4_out));
  Pull_Resistor pull_resistor_5 (.node(controlled_buffer_5_out));
  Pull_Resistor pull_resistor_6 (.node(pull_resistor_6_node));
  assign pull_resistor_6_node = or_6_out ? and_2_out : 5'bz;  // Controlled_Buffer controlled_buffer_6
  or or_7 (JMP, decoder_1_out1, pull_resistor_6_node[0], pull_resistor_6_node[1], pull_resistor_6_node[2], pull_resistor_6_node[3], pull_resistor_6_node[4], controlled_buffer_1_out, controlled_buffer_2_out, controlled_buffer_3_out, controlled_buffer_4_out, controlled_buffer_5_out);

  // Notes on the sheet:
  //   ADD
  //   SUB
  //   INC/DEC
  //   CMP
endmodule

module PC (
  input  PCOUTEN,
  input  PCLOAD,
  input  [15:0] PCLOADADDR1,
  input  [15:0] PCLOADADDR2,
  input  RESET,
  input  HALT,
  input  CONT,
  input  PCCLKIN,
  output [15:0] PCMOVOUT,
  output [15:0] PCOUT,
  output PCOVERFLOW
);

  wire not_1_out, pull_resistor_3_node, s_r_ff_1_qn;
  wire [15:0] or_1_out;

  Pull_Resistor pull_resistor_1 (.node(PCLOADADDR1));
  Pull_Resistor pull_resistor_2 (.node(PCLOADADDR2));
  assign PCMOVOUT = PCOUTEN ? PCOUT : 16'bz;  // Controlled_Buffer controlled_buffer_1
  assign or_1_out = PCLOADADDR1 | PCLOADADDR2;  // OR_Gate or_1, 16 bits wide
  S_R_Flip_Flop s_r_ff_1 (.S(HALT), .clk(PCCLKIN), .R(CONT), .Qn(s_r_ff_1_qn), .reset(RESET));  // open: Q, preset, en
  not not_1 (not_1_out, PCLOAD);
  Pull_Resistor pull_resistor_3 (.node(pull_resistor_3_node));
  Counter #(.width(16), .max('hffff), .ongoal("stay")) counter_1 (
    .load(PCLOAD), .D(or_1_out), .count(not_1_out), .Q(PCOUT), .carry(PCOVERFLOW),
    .clk(pull_resistor_3_node), .clr(RESET));
  assign pull_resistor_3_node = s_r_ff_1_qn ? PCCLKIN : 1'bz;  // Controlled_Buffer controlled_buffer_2
endmodule

module ROM (
  input  [15:0] ROMIN,
  output [31:0] ROMOUT
);

  ROM_part #(.addrWidth(16), .dataWidth(32)) rom_1 (.addr(ROMIN), .data(ROMOUT));  // open: sel

  // Notes on the sheet:
  //   contents of rom_1 (hex, n*v repeats v):
  //   e0000000 e2400000 e000ffff e2500000 e0000100 e0103493 e000002d e0103494 e0000033 e0103495 e0000032
  //   e0103496 e0000037 e0103497 e0000036 e0103498 e0000038 e0103499 e0000030 e010349b e0000031 e010349c
  //   e0000032 e010349d e0000033 e010349e e0000034 e010349f e0000035 e01034a0 e0000036 e01034a1 e0000037
  //   e01034a2 e0000038 e01034a3 e0000039 e01034a4 e0000061 e01034a5 e0000062 e01034a6 e0000063 e01034a7
  //   e0000064 e01034a8 e0000065 e01034a9 e0000066 e01034aa e000006e e01034ac e000006f e01034ad e0000074
  //   e01034ae e0000020 e01034af e0000066 e01034b0 e000006f e01034b1 e0000075 e01034b2 e000006e e01034b3
  //   e0000064 e01034b4 e000003f e01034b6 e0000052 e01034b7 e0000042 e01034b8 e000005a e01034b9 e0000050
  //   e01034bb e0000049 e01034bc e0000044 e01034bd e0000020 e01034be e0000050 e01034bf e0000050 e01034c0
  //   e0000049 e01034c1 e0000044 e01034c2 e0000020 e01034c3 e0000053 e01034c4 e0000054 e01034c5 e0000020
  //   e01034c6 e000004e e01034c7 e0000041 e01034c8 e000004d e01034c9 e0000045 e01034ca e0000020 e01034cc
  //   e0000025 e01034cd e0000064 e01034ce e0000020 e01034cf e0000020 e01034d0 e0000020 e01034d1 e0000025
  //   e01034d2 e0000064 e01034d3 e0000020 e01034d4 e0000020 e01034d5 e0000020 e01034d6 e0000025 e01034d7
  //   e0000063 e01034d8 e0000020 e01034d9 e0000020 e01034da e0000052 e01034dc e0000049 e01034dd e0000053
  //   e01034de e000004b e01034df e0000059 e01034e0 e0000020 e01034e1 e000004f e01034e2 e0000053 e01034e3
  //   e0000020 e01034e4 e0000076 e01034e5 e0000033 e01034e6 e0000020 e01034e7 e0000073 e01034e8 e0000068
  //   e01034e9 e0000065 e01034ea e000006c e01034eb e000006c e01034ec e000002e e01034ed e0000020 e01034ee
  //   e0000020 e01034ef e0000054 e01034f0 e0000079 e01034f1 e0000070 e01034f2 e0000065 e01034f3 e0000020
  //   e01034f4 e0000027 e01034f5 e0000068 e01034f6 e0000065 e01034f7 e000006c e01034f8 e0000070 e01034f9
  //   e0000027 e01034fa e000002e e01034fb e0000068 e01034fd e0000065 e01034fe e000006c e01034ff e0000070
  //   e0103500 e0000068 e0103502 e0000065 e0103503 e000006c e0103504 e0000070 e0103505 e0000020 e0103506
  //   e0000070 e0103507 e0000073 e0103508 e0000020 e0103509 e000006c e010350a e0000073 e010350b e0000020
  //   e010350c e0000063 e010350d e0000061 e010350e e0000074 e010350f e0000020 e0103510 e000006d e0103511
  //   e000006b e0103512 e0000066 e0103513 e0000069 e0103514 e000006c e0103515 e0000065 e0103516 e0000020
  //   e0103517 e000006d e0103518 e000006b e0103519 e0000064 e010351a e0000069 e010351b e0000072 e010351c
  //   e0000020 e010351d e0000070 e010351e e0000069 e010351f e0000070 e0103520 e0000065 e0103521 e0000020
  //   e0103522 e0000077 e0103523 e0000072 e0103524 e0000069 e0103525 e0000074 e0103526 e0000065 e0103527
  //   e0000020 e0103528 e0000065 e0103529 e0000078 e010352a e0000069 e010352b e0000074 e010352c e0000070
  //   e010352e e0000073 e010352f e000006c e0103531 e0000073 e0103532 e0000063 e0103534 e0000061 e0103535
  //   e0000074 e0103536 e000006d e0103538 e000006b e0103539 e0000066 e010353a e0000069 e010353b e000006c
  //   e010353c e0000065 e010353d e000006d e010353f e000006b e0103540 e0000064 e0103541 e0000069 e0103542
  //   e0000072 e0103543 e0000064 e0103545 e0000069 e0103546 e0000072 e0103547 e0000066 e0103549 e0000069
  //   e010354a e000006c e010354b e0000065 e010354c e0000063 e010354e e0000072 e010354f e0000065 e0103550
  //   e0000061 e0103551 e0000074 e0103552 e0000065 e0103553 e0000064 e0103554 e0000020 e0103555 e0000025
  //   e0103556 e0000073 e0103557 e0000020 e0103558 e0000025 e0103559 e0000073 e010355a e0000020 e010355b
  //   e0000028 e010355c e0000069 e010355d e000006e e010355e e000006f e010355f e0000020 e0103560 e0000025
  //   e0103561 e0000064 e0103562 e0000029 e0103563 e000000a e0103564 e0000063 e0103566 e0000072 e0103567
  //   e0000065 e0103568 e0000061 e0103569 e0000074 e010356a e0000065 e010356b e0000020 e010356c e0000066
  //   e010356d e0000061 e010356e e0000069 e010356f e000006c e0103570 e0000065 e0103571 e0000064 e0103572
  //   e0000077 e0103574 e0000072 e0103575 e0000069 e0103576 e0000074 e0103577 e0000065 e0103578 e0000077
  //   e010357a e0000072 e010357b e000006f e010357c e0000074 e010357d e0000065 e010357e e0000020 e010357f
  //   e0000025 e0103580 e0000064 e0103581 e000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
endmodule

module RAM (
  input  [15:0] RAMADDRIN,
  input  [15:0] RAMDATAIN,
  input  RESET,
  input  RAMLOAD,
  input  [15:0] RAMPAGEIN,
  input  RAMSTORE,
  input  RAMCLKIN,
  output [15:0] RAMDATAOUT
);

  wire comparator_1_eq, comparator_2_eq, comparator_3_eq, comparator_4_eq, comparator_5_eq, comparator_6_eq,
       comparator_7_eq, comparator_8_eq, comparator_9_eq, comparator_10_eq;

  Comparator #(.width(16)) comparator_1 (.a(RAMPAGEIN), .b({16{1'b0}}), .eq(comparator_1_eq));  // open: gt, lt
  Comparator #(.width(16)) comparator_2 (.a(RAMPAGEIN), .b(16'h1), .eq(comparator_2_eq));  // open: gt, lt
  Comparator #(.width(16)) comparator_3 (.a(RAMPAGEIN), .b(16'h2), .eq(comparator_3_eq));  // open: gt, lt
  Comparator #(.width(16)) comparator_4 (.a(RAMPAGEIN), .b(16'h3), .eq(comparator_4_eq));  // open: gt, lt
  Comparator #(.width(16)) comparator_5 (.a(RAMPAGEIN), .b(16'h4), .eq(comparator_5_eq));  // open: gt, lt
  Comparator #(.width(16)) comparator_6 (.a(RAMPAGEIN), .b(16'h5), .eq(comparator_6_eq));  // open: gt, lt
  Comparator #(.width(16)) comparator_7 (.a(RAMPAGEIN), .b(16'h6), .eq(comparator_7_eq));  // open: gt, lt
  Comparator #(.width(16)) comparator_8 (.a(RAMPAGEIN), .b(16'h7), .eq(comparator_8_eq));  // open: gt, lt
  Comparator #(.width(16)) comparator_9 (.a(RAMPAGEIN), .b(16'h8), .eq(comparator_9_eq));  // open: gt, lt
  Comparator #(.width(16)) comparator_10 (.a(RAMPAGEIN), .b(16'h9), .eq(comparator_10_eq));  // open: gt, lt
  RAM_part #(.addrWidth(16), .dataWidth(16), .bus("separate")) ram_1 (
    .addr(RAMADDRIN), .din(RAMDATAIN), .data(RAMDATAOUT), .str(RAMSTORE), .sel(comparator_1_eq),
    .clk(RAMCLKIN), .ld(RAMLOAD), .clr(RESET));
  RAM_part #(.addrWidth(16), .dataWidth(16), .bus("separate")) ram_2 (
    .addr(RAMADDRIN), .din(RAMDATAIN), .data(RAMDATAOUT), .str(RAMSTORE), .sel(comparator_2_eq),
    .clk(RAMCLKIN), .ld(RAMLOAD), .clr(RESET));
  RAM_part #(.addrWidth(16), .dataWidth(16), .bus("separate")) ram_3 (
    .addr(RAMADDRIN), .din(RAMDATAIN), .data(RAMDATAOUT), .str(RAMSTORE), .sel(comparator_3_eq),
    .clk(RAMCLKIN), .ld(RAMLOAD), .clr(RESET));
  RAM_part #(.addrWidth(16), .dataWidth(16), .bus("separate")) ram_4 (
    .addr(RAMADDRIN), .din(RAMDATAIN), .data(RAMDATAOUT), .str(RAMSTORE), .sel(comparator_4_eq),
    .clk(RAMCLKIN), .ld(RAMLOAD), .clr(RESET));
  RAM_part #(.addrWidth(16), .dataWidth(16), .bus("separate")) ram_5 (
    .addr(RAMADDRIN), .din(RAMDATAIN), .data(RAMDATAOUT), .str(RAMSTORE), .sel(comparator_5_eq),
    .clk(RAMCLKIN), .ld(RAMLOAD), .clr(RESET));
  RAM_part #(.addrWidth(16), .dataWidth(16), .bus("separate")) ram_6 (
    .addr(RAMADDRIN), .din(RAMDATAIN), .data(RAMDATAOUT), .str(RAMSTORE), .sel(comparator_6_eq),
    .clk(RAMCLKIN), .ld(RAMLOAD), .clr(RESET));
  RAM_part #(.addrWidth(16), .dataWidth(16), .bus("separate")) ram_7 (
    .addr(RAMADDRIN), .din(RAMDATAIN), .data(RAMDATAOUT), .str(RAMSTORE), .sel(comparator_7_eq),
    .clk(RAMCLKIN), .ld(RAMLOAD), .clr(RESET));
  RAM_part #(.addrWidth(16), .dataWidth(16), .bus("separate")) ram_8 (
    .addr(RAMADDRIN), .din(RAMDATAIN), .data(RAMDATAOUT), .str(RAMSTORE), .sel(comparator_8_eq),
    .clk(RAMCLKIN), .ld(RAMLOAD), .clr(RESET));
  RAM_part #(.addrWidth(16), .dataWidth(16), .bus("separate")) ram_9 (
    .addr(RAMADDRIN), .din(RAMDATAIN), .data(RAMDATAOUT), .str(RAMSTORE), .sel(comparator_9_eq),
    .clk(RAMCLKIN), .ld(RAMLOAD), .clr(RESET));
  RAM_part #(.addrWidth(16), .dataWidth(16), .bus("separate")) ram_10 (
    .addr(RAMADDRIN), .din(RAMDATAIN), .data(RAMDATAOUT), .str(RAMSTORE), .sel(comparator_10_eq),
    .clk(RAMCLKIN), .ld(RAMLOAD), .clr(RESET));
endmodule

module SP (
  input  [1:0] SPMODE,
  input  [15:0] SPLOADADDR,
  input  RESET,
  input  SPCLKIN,
  output [15:0] SPOUT
);

  wire and_1_out;
  wire [15:0] bit_extender_1_out, counter_1_q, subtractor_1_out, subtractor_2_out;

  Subtractor #(.width(16)) subtractor_1 (.a({16{1'b1}}), .b(SPLOADADDR), .out(subtractor_1_out));  // open: bin, bout
  Counter #(.width(16), .max('hffff), .ongoal("stay")) counter_1 (
    .load(SPMODE[0]), .D(subtractor_1_out), .count(SPMODE[1]), .Q(counter_1_q), .clk(SPCLKIN), .clr(RESET));  // open: carry
  and and_1 (and_1_out, SPMODE[0], SPMODE[1]);
  assign bit_extender_1_out = {{15{1'b0}}, and_1_out};  // Bit_Extender bit_extender_1
  Subtractor #(.width(16)) subtractor_2 (.a({16{1'b1}}), .b(counter_1_q), .out(subtractor_2_out));  // open: bin, bout
  Adder #(.width(16)) adder_1 (.a(bit_extender_1_out), .b(subtractor_2_out), .out(SPOUT));  // open: cin, cout

  // Notes on the sheet:
  //   01 = LOAD
  //   10 = PUSH
  //   11 = POP
endmodule

module CU (
  input  [31:0] CUROMIN,
  output REGINEN1,
  output REGINEN2,
  output REGOUTEN1,
  output REGOUTEN2,
  output REGOUTEN3,
  output REGOUTEN4,
  output REGMOV,
  output ALUINEN,
  output ALU32INEN,
  output ALUOUTEN,
  output [3:0] ALUOPSEL,
  output CUIMMEDIATE,
  output [1:0] REGSELMODESEL,
  output ALU32OUTEN,
  output RAMLOAD,
  output RAMSTORE,
  output [2:0] RAMMODESEL,
  output PCLOAD,
  output [3:0] JMPTYPE,
  output PCOUT,
  output [1:0] SPMODE,
  output RESET,
  output PAGEOUT,
  output PAGELOAD,
  output RAMOFFSETEN,
  output SPOUT,
  output STATEOUTEN,
  output out_29,
  output [15:0] CUIMMEDIATEOUT
);

  wire and_1_out, comparator_1_eq, comparator_1_lt, comparator_2_eq, comparator_3_eq, comparator_4_eq;
  wire [31:5] rom_6_data;

  and and_1 (and_1_out, ~ALUOUTEN, CUIMMEDIATE);  // AND_Gate
  Comparator #(.width(4), .mode("unsigned")) comparator_1 (
    .a(CUROMIN[31:28]), .b(4'b1100), .eq(comparator_1_eq), .lt(comparator_1_lt));  // open: gt
  Comparator #(.width(4), .mode("unsigned")) comparator_2 (
    .a(CUROMIN[31:28]), .b(4'b1101), .eq(comparator_2_eq));  // open: gt, lt
  Comparator #(.width(4), .mode("unsigned")) comparator_3 (
    .a(CUROMIN[31:28]), .b(4'b1110), .eq(comparator_3_eq));  // open: gt, lt
  Comparator #(.width(4), .mode("unsigned")) comparator_4 (
    .a(CUROMIN[31:28]), .b(4'b1111), .eq(comparator_4_eq));  // open: gt, lt
  assign CUIMMEDIATEOUT = and_1_out ? CUROMIN[15:0] : 16'bz;  // Controlled_Buffer controlled_buffer_1
  ROM_part #(.addrWidth(4), .dataWidth(32)) rom_1 (
    .addr(CUROMIN[31:28]),
    .data({RESET, SPMODE, PCOUT, JMPTYPE, PCLOAD, RAMMODESEL, RAMSTORE, RAMLOAD, ALU32OUTEN, REGSELMODESEL, CUIMMEDIATE, ALUOPSEL, ALUOUTEN, ALU32INEN, ALUINEN, REGMOV, REGOUTEN4, REGOUTEN3, REGOUTEN2, REGOUTEN1, REGINEN2, REGINEN1}),
    .sel(comparator_1_lt));
  ROM_part #(.addrWidth(4), .dataWidth(32)) rom_2 (
    .addr(CUROMIN[27:24]),
    .data({RESET, SPMODE, PCOUT, JMPTYPE, PCLOAD, RAMMODESEL, RAMSTORE, RAMLOAD, ALU32OUTEN, REGSELMODESEL, CUIMMEDIATE, ALUOPSEL, ALUOUTEN, ALU32INEN, ALUINEN, REGMOV, REGOUTEN4, REGOUTEN3, REGOUTEN2, REGOUTEN1, REGINEN2, REGINEN1}),
    .sel(comparator_1_eq));
  ROM_part #(.addrWidth(4), .dataWidth(32)) rom_3 (
    .addr(CUROMIN[27:24]),
    .data({RESET, SPMODE, PCOUT, JMPTYPE, PCLOAD, RAMMODESEL, RAMSTORE, RAMLOAD, ALU32OUTEN, REGSELMODESEL, CUIMMEDIATE, ALUOPSEL, ALUOUTEN, ALU32INEN, ALUINEN, REGMOV, REGOUTEN4, REGOUTEN3, REGOUTEN2, REGOUTEN1, REGINEN2, REGINEN1}),
    .sel(comparator_2_eq));
  ROM_part #(.dataWidth(32)) rom_4 (
    .addr(CUROMIN[27:20]),
    .data({RESET, SPMODE, PCOUT, JMPTYPE, PCLOAD, RAMMODESEL, RAMSTORE, RAMLOAD, ALU32OUTEN, REGSELMODESEL, CUIMMEDIATE, ALUOPSEL, ALUOUTEN, ALU32INEN, ALUINEN, REGMOV, REGOUTEN4, REGOUTEN3, REGOUTEN2, REGOUTEN1, REGINEN2, REGINEN1}),
    .sel(comparator_3_eq));
  ROM_part #(.addrWidth(12), .dataWidth(32)) rom_5 (
    .addr(CUROMIN[27:16]),
    .data({RESET, SPMODE, PCOUT, JMPTYPE, PCLOAD, RAMMODESEL, RAMSTORE, RAMLOAD, ALU32OUTEN, REGSELMODESEL, CUIMMEDIATE, ALUOPSEL, ALUOUTEN, ALU32INEN, ALUINEN, REGMOV, REGOUTEN4, REGOUTEN3, REGOUTEN2, REGOUTEN1, REGINEN2, REGINEN1}),
    .sel(comparator_4_eq));
  ROM_part #(.addrWidth(4), .dataWidth(32)) rom_6 (
    .addr(CUROMIN[31:28]), .data({rom_6_data, STATEOUTEN, SPOUT, RAMOFFSETEN, PAGELOAD, PAGEOUT}),
    .sel(comparator_1_lt));
  ROM_part #(.addrWidth(4), .dataWidth(32)) rom_7 (
    .addr(CUROMIN[27:24]), .data({rom_6_data, STATEOUTEN, SPOUT, RAMOFFSETEN, PAGELOAD, PAGEOUT}),
    .sel(comparator_1_eq));
  ROM_part #(.addrWidth(4), .dataWidth(32)) rom_8 (
    .addr(CUROMIN[27:24]), .data({rom_6_data, STATEOUTEN, SPOUT, RAMOFFSETEN, PAGELOAD, PAGEOUT}),
    .sel(comparator_2_eq));
  ROM_part #(.dataWidth(32)) rom_9 (
    .addr(CUROMIN[27:20]), .data({rom_6_data, STATEOUTEN, SPOUT, RAMOFFSETEN, PAGELOAD, PAGEOUT}),
    .sel(comparator_3_eq));
  ROM_part #(.addrWidth(12), .dataWidth(32)) rom_10 (
    .addr(CUROMIN[27:16]), .data({rom_6_data, STATEOUTEN, SPOUT, RAMOFFSETEN, PAGELOAD, PAGEOUT}),
    .sel(comparator_4_eq));

  // Notes on the sheet:
  //   LOW
  //   contents of rom_1 (hex, n*v repeats v):
  //   0 8295 8695 8a95 8e95 9295 9695 9e95 a295 a695 aa95 ae95
  //   contents of rom_2 (hex, n*v repeats v):
  //   51 1a91 3291 2013f 2053f 2093f 20d3f 2113f 2153f 21933 21d3f 2213f 2253f 2293f 22d3f 23133
  //   contents of rom_3 (hex, n*v repeats v):
  //   80014 140011 73 94 13c 80014 140011
  //   contents of rom_4 (hex, n*v repeats v):
  //   1c001 290004 358001 490004 10018001 810004 1810004 2810004 3810004 4810004 5810004 6810004 7810004
  //   8810004 9810004 a810004 b810004 c810004 d810004 e810004 f810004 14084 1c285 1c685 1ca85 1ce85 1d285
  //   1d685 1da85 1de85 1e285 1e685 1ea85 1ee85 1f285 18001 10004 20010004 40690004 60758001 18001 18001
  //   contents of rom_5 (hex, n*v repeats v):
  //   804000 1804000 2804000 3804000 4804000 5804000 6804000 7804000 8804000 9804000 a804000 b804000
  //   c804000 d804000 e804000 f804000 40580000 60758000
  //   HIGH
  //   contents of rom_8 (hex, n*v repeats v):
  //   5*0 4 4
  //   contents of rom_9 (hex, n*v repeats v):
  //   35*0 1 2 0 0 0 10 8
endmodule

module REGSEL (
  input  [1:0] REGSELMODESEL,
  input  [31:0] REGSELINSTRIN,
  output [3:0] REGINSEL1,
  output [3:0] REGINSEL2,
  output [3:0] REGOUTSEL1,
  output [3:0] REGOUTSEL2,
  output [3:0] REGOUTSEL3,
  output [3:0] REGOUTSEL4
);

  wire [3:0] demultiplexer_1_out1, demultiplexer_2_out0, demultiplexer_2_out1, demultiplexer_3_out0,
       demultiplexer_3_out1, demultiplexer_3_out2, demultiplexer_3_out3;

  assign REGINSEL1 = demultiplexer_2_out0 | demultiplexer_1_out1 | demultiplexer_3_out3;  // OR_Gate or_1, 4 bits wide
  Demultiplexer #(.select(2), .width(4), .enable("false")) demultiplexer_1 (
    .out1(demultiplexer_1_out1), .in(REGSELINSTRIN[27:24]), .sel(REGSELMODESEL));  // open: out0, out2, out3
  Adder #(.width(4)) adder_1 (.a(REGINSEL1), .b(4'b0001), .out(REGINSEL2));  // open: cin, cout
  Demultiplexer #(.select(2), .width(4), .enable("false")) demultiplexer_2 (
    .out0(demultiplexer_2_out0), .out1(demultiplexer_2_out1), .in(REGSELINSTRIN[23:20]), .sel(REGSELMODESEL));  // open: out2, out3
  assign REGOUTSEL1 = demultiplexer_2_out0 | demultiplexer_2_out1 | demultiplexer_3_out2 | demultiplexer_3_out3;  // OR_Gate or_2, 4 bits wide
  Adder #(.width(4)) adder_2 (.a(REGOUTSEL1), .b(4'b0001), .out(REGOUTSEL2));  // open: cin, cout
  Demultiplexer #(.select(2), .width(4), .enable("false")) demultiplexer_3 (
    .out0(demultiplexer_3_out0), .out1(demultiplexer_3_out1), .out2(demultiplexer_3_out2),
    .out3(demultiplexer_3_out3), .in(REGSELINSTRIN[19:16]), .sel(REGSELMODESEL));
  assign REGOUTSEL3 = demultiplexer_3_out0 | demultiplexer_3_out1;  // OR_Gate or_3, 4 bits wide
  Adder #(.width(4)) adder_3 (.a(REGOUTSEL3), .b(4'b0001), .out(REGOUTSEL4));  // open: cin, cout

  // Notes on the sheet:
  //   00 = binary op
  //   01 = ternary op
  //   10 = unary op, reg is source
  //   11 = unary op, reg is drain and source
endmodule

module ALUREG (
  input  [15:0] ALUIN1,
  input  [31:0] ALUIN2,
  input  [31:0] ALUIMMEDIATEIN,
  input  ALUIMMEDIATEIN_2,
  input  [15:0] REGDATAIN1,
  input  [15:0] REGDATAIN2,
  input  [15:0] REGDATAIN3,
  input  [15:0] REGDATAIN4,
  output [15:0] ALUOUT1,
  output [15:0] ALUOUT2,
  output [31:0] ALU32IN1,
  output [31:0] ALU32IN2,
  output [15:0] REGDATAOUT1,
  output [15:0] REGDATAOUT2
);

  Multiplexer #(.width(16), .enable("false")) multiplexer_1 (
    .in0(REGDATAIN3), .in1(ALUIMMEDIATEIN[15:0]), .out(ALUOUT2), .sel(ALUIMMEDIATEIN_2));

  assign ALU32IN1 = {REGDATAIN1, REGDATAIN2};
  assign ALU32IN2 = {REGDATAIN3, REGDATAIN4};
  assign ALUIN2[31:16] = ALUIN1;
  assign ALUOUT1 = REGDATAIN1;
  assign REGDATAOUT1 = ALUIN1;
  assign REGDATAOUT2 = ALUIN2[15:0];
endmodule

module CU_DEVTOOL (
  input  REGINEN1,
  input  REGINEN2,
  input  REGOUTEN1,
  input  REGOUTEN2,
  input  REGOUTEN3,
  input  REGOUTEN4,
  input  REGMOV,
  input  ALUINEN,
  input  ALU32INEN,
  input  ALUOUTEN,
  input  [3:0] ALUOPSEL,
  input  CUIMMEDIATE,
  input  [1:0] REGSELMODESEL,
  input  ALU32OUTEN,
  input  RAMLOAD,
  input  RAMSTORE,
  input  [2:0] RAMMODESEL,
  input  PCLOAD,
  input  [3:0] JMPTYPE,
  input  PCOUT,
  input  [1:0] SPMODE,
  input  RESET,
  input  PAGEOUT,
  input  PAGELOAD,
  input  RAMOFFSETEN,
  input  SPOUT,
  input  STATEOUTEN,
  input  in_28
);

  wire [3:0] pull_resistor_2_node_2, pull_resistor_2_node_3, pull_resistor_2_node_4, pull_resistor_2_node_5,
       pull_resistor_2_node_6;
  wire [11:5] pull_resistor_2_node;

  Hex_Digit_Display hex_digit_display_1 (.value({RESET, SPMODE, PCOUT}));  // open: dp
  Hex_Digit_Display hex_digit_display_2 (.value(pull_resistor_2_node_6));  // open: dp
  Hex_Digit_Display hex_digit_display_3 (.value({PCLOAD, RAMMODESEL}));  // open: dp
  Hex_Digit_Display hex_digit_display_4 (.value(JMPTYPE));  // open: dp
  Hex_Digit_Display hex_digit_display_5 (.value(pull_resistor_2_node_5));  // open: dp
  Hex_Digit_Display hex_digit_display_6 (.value(pull_resistor_2_node_4));  // open: dp
  Hex_Digit_Display hex_digit_display_7 (.value({REGSELMODESEL[0], CUIMMEDIATE, ALUOPSEL[3:2]}));  // open: dp
  Hex_Digit_Display hex_digit_display_8 (.value({RAMSTORE, RAMLOAD, ALU32OUTEN, REGSELMODESEL[1]}));  // open: dp
  Hex_Digit_Display hex_digit_display_9 (.value(pull_resistor_2_node_2));  // open: dp
  Hex_Digit_Display hex_digit_display_10 (.value(pull_resistor_2_node_3));  // open: dp
  Hex_Digit_Display hex_digit_display_11 (.value({ALUOPSEL[1:0], ALUOUTEN, ALU32INEN}));  // open: dp
  Hex_Digit_Display hex_digit_display_12 (.value({ALUINEN, REGMOV, REGOUTEN4, REGOUTEN3}));  // open: dp
  Hex_Digit_Display hex_digit_display_13 (.value({pull_resistor_2_node[7:5], STATEOUTEN}));  // open: dp
  Hex_Digit_Display hex_digit_display_14 (.value(pull_resistor_2_node[11:8]));  // open: dp
  Hex_Digit_Display hex_digit_display_15 (.value({REGOUTEN2, REGOUTEN1, REGINEN2, REGINEN1}));  // open: dp
  Pull_Resistor pull_resistor_1 (.node({RESET, SPMODE, PCOUT, JMPTYPE, PCLOAD, RAMMODESEL, RAMSTORE, RAMLOAD, ALU32OUTEN, REGSELMODESEL, CUIMMEDIATE, ALUOPSEL, ALUOUTEN, ALU32INEN, ALUINEN, REGMOV, REGOUTEN4, REGOUTEN3, REGOUTEN2, REGOUTEN1, REGINEN2, REGINEN1}));
  Hex_Digit_Display hex_digit_display_16 (.value({SPOUT, RAMOFFSETEN, PAGELOAD, PAGEOUT}));  // open: dp
  Pull_Resistor pull_resistor_2 (.node({pull_resistor_2_node_6, pull_resistor_2_node_5, pull_resistor_2_node_4, pull_resistor_2_node_3, pull_resistor_2_node_2, pull_resistor_2_node, STATEOUTEN, SPOUT, RAMOFFSETEN, PAGELOAD, PAGEOUT}));
endmodule

module RAMREG (
  input  PAGEOUT,
  input  PAGELOAD,
  input  [1:0] SPMODE,
  input  [2:0] RAMMODESEL,
  input  SPOUT,
  input  CLKIN,
  input  RESET,
  input  [15:0] REGDATAIN1,
  input  [15:0] REGDATAIN2,
  input  RAMOFFSETEN,
  input  [15:0] REGDATAIN3,
  input  [15:0] RAMDATAOUT,
  input  [15:0] REGDATAIN4,
  input  [31:0] RAMIMMEDIATEIN,
  output [15:0] REGDATAOUT1,
  output [15:0] REGDATAOUT2,
  output [15:0] RAMDATAIN,
  output [15:0] RAMADDROUT,
  output [15:0] PAGEOUT_2
);

  wire [15:0] multiplexer_2_out, multiplexer_3_out, sp_1_spout;

  assign REGDATAOUT1 = SPOUT ? sp_1_spout : 16'bz;  // Controlled_Buffer controlled_buffer_1
  PAGE page_1 (
    .PAGEOUT(PAGEOUT), .PAGEMOVEOUT(REGDATAOUT1), .PAGEIN(REGDATAIN1), .PAGELOAD(PAGELOAD),
    .PAGEOUT_2(PAGEOUT_2), .CLKIN(CLKIN), .RESET(RESET));
  SP sp_1 (.SPLOADADDR(REGDATAIN1), .SPOUT(sp_1_spout), .RESET(RESET), .SPCLKIN(CLKIN), .SPMODE(SPMODE));
  Multiplexer #(.select(3), .width(16), .enable("false")) multiplexer_1 (
    .in0(REGDATAIN3), .in1(REGDATAIN1), .in2(REGDATAIN1), .in4(RAMIMMEDIATEIN[15:0]),
    .in5(RAMIMMEDIATEIN[15:0]), .in6(REGDATAIN1), .out(RAMDATAIN), .sel(RAMMODESEL));  // open: in3, in7
  Multiplexer #(.select(3), .width(16), .enable("false")) multiplexer_2 (
    .in0(REGDATAIN1), .in1(REGDATAIN3), .in2(RAMIMMEDIATEIN[15:0]), .in3(RAMIMMEDIATEIN[15:0]),
    .in4(REGDATAIN1), .in5(sp_1_spout), .in6(sp_1_spout), .in7(sp_1_spout), .out(multiplexer_2_out),
    .sel(RAMMODESEL));
  Demultiplexer #(.select(3), .width(16), .tristate("true"), .enable("false")) demultiplexer_1 (
    .out1(REGDATAOUT1), .out3(REGDATAOUT1), .out7(REGDATAOUT1), .in(RAMDATAOUT), .sel(RAMMODESEL));  // open: out0, out2, out4, out5, out6
  Adder #(.width(16)) adder_1 (.a(multiplexer_2_out), .b(multiplexer_3_out), .out(RAMADDROUT));  // open: cin, cout
  Multiplexer #(.width(16), .enable("false")) multiplexer_3 (
    .in0({16{1'b0}}), .in1(RAMIMMEDIATEIN[15:0]), .out(multiplexer_3_out), .sel(RAMOFFSETEN));

  // Notes on the sheet:
  //   000 = STOR
  //   001 = LDR
  //   010 = STOD
  //   011 = LDD
  //   100 = STOI
  //   101 = PUSHI
  //   110 = PUSH
  //   111 = POP
endmodule

module JMPGATE (
  input  PCLOADIN,
  input  [3:0] JMPTYPE,
  input  [13:0] STATUSIN,
  input  KBAVAILABLEIN,
  input  STATEOUTEN,
  output PCLOADOUT,
  output [15:0] STATEOUT
);

  wire controlled_buffer_2_out, controlled_buffer_3_out, controlled_buffer_4_out, controlled_buffer_5_out,
       controlled_buffer_6_out, controlled_buffer_7_out, controlled_buffer_8_out, controlled_buffer_9_out,
       controlled_buffer_10_out, controlled_buffer_11_out, controlled_buffer_12_out,
       controlled_buffer_13_out, controlled_buffer_14_out, controlled_buffer_15_out,
       controlled_buffer_16_out, controlled_buffer_17_out, decoder_1_out0, decoder_1_out1, decoder_1_out2,
       decoder_1_out3, decoder_1_out4, decoder_1_out5, decoder_1_out6, decoder_1_out7, decoder_1_out8,
       decoder_1_out9, decoder_1_out10, decoder_1_out11, decoder_1_out12, decoder_1_out13, decoder_1_out14,
       decoder_1_out15;
  wire [15:0] bit_extender_1_out;

  assign bit_extender_1_out = {{2{1'b0}}, STATUSIN};  // Bit_Extender bit_extender_1
  assign STATEOUT = STATEOUTEN ? bit_extender_1_out : 16'bz;  // Controlled_Buffer controlled_buffer_1
  assign controlled_buffer_2_out = decoder_1_out0 ? 1'b1 : 1'bz;  // Controlled_Buffer controlled_buffer_2
  assign controlled_buffer_3_out = decoder_1_out1 ? STATUSIN[0] : 1'bz;  // Controlled_Buffer controlled_buffer_3
  assign controlled_buffer_4_out = decoder_1_out2 ? STATUSIN[1] : 1'bz;  // Controlled_Buffer controlled_buffer_4
  assign controlled_buffer_5_out = decoder_1_out3 ? STATUSIN[2] : 1'bz;  // Controlled_Buffer controlled_buffer_5
  assign controlled_buffer_6_out = decoder_1_out4 ? STATUSIN[3] : 1'bz;  // Controlled_Buffer controlled_buffer_6
  assign controlled_buffer_7_out = decoder_1_out5 ? STATUSIN[4] : 1'bz;  // Controlled_Buffer controlled_buffer_7
  assign controlled_buffer_8_out = decoder_1_out6 ? STATUSIN[5] : 1'bz;  // Controlled_Buffer controlled_buffer_8
  assign controlled_buffer_9_out = decoder_1_out7 ? STATUSIN[6] : 1'bz;  // Controlled_Buffer controlled_buffer_9
  assign controlled_buffer_10_out = decoder_1_out8 ? STATUSIN[7] : 1'bz;  // Controlled_Buffer controlled_buffer_10
  Decoder #(.select(4), .disabled(0)) decoder_1 (
    .out0(decoder_1_out0), .out1(decoder_1_out1), .out2(decoder_1_out2), .out3(decoder_1_out3),
    .out4(decoder_1_out4), .out5(decoder_1_out5), .out6(decoder_1_out6), .out7(decoder_1_out7),
    .out8(decoder_1_out8), .out9(decoder_1_out9), .out10(decoder_1_out10), .out11(decoder_1_out11),
    .out12(decoder_1_out12), .out13(decoder_1_out13), .out14(decoder_1_out14), .out15(decoder_1_out15),
    .sel(JMPTYPE), .en(PCLOADIN));
  assign controlled_buffer_11_out = decoder_1_out9 ? STATUSIN[8] : 1'bz;  // Controlled_Buffer controlled_buffer_11
  assign controlled_buffer_12_out = decoder_1_out10 ? STATUSIN[9] : 1'bz;  // Controlled_Buffer controlled_buffer_12
  assign controlled_buffer_13_out = decoder_1_out11 ? STATUSIN[10] : 1'bz;  // Controlled_Buffer controlled_buffer_13
  assign controlled_buffer_14_out = decoder_1_out12 ? STATUSIN[11] : 1'bz;  // Controlled_Buffer controlled_buffer_14
  Pull_Resistor pull_resistor_1 (.node(controlled_buffer_2_out));
  assign controlled_buffer_15_out = decoder_1_out13 ? STATUSIN[12] : 1'bz;  // Controlled_Buffer controlled_buffer_15
  assign controlled_buffer_16_out = decoder_1_out14 ? STATUSIN[13] : 1'bz;  // Controlled_Buffer controlled_buffer_16
  assign controlled_buffer_17_out = decoder_1_out15 ? KBAVAILABLEIN : 1'bz;  // Controlled_Buffer controlled_buffer_17
  Pull_Resistor pull_resistor_2 (.node(controlled_buffer_3_out));
  Pull_Resistor pull_resistor_3 (.node(controlled_buffer_4_out));
  Pull_Resistor pull_resistor_4 (.node(controlled_buffer_5_out));
  Pull_Resistor pull_resistor_5 (.node(controlled_buffer_6_out));
  Pull_Resistor pull_resistor_6 (.node(controlled_buffer_7_out));
  Pull_Resistor pull_resistor_7 (.node(controlled_buffer_8_out));
  Pull_Resistor pull_resistor_8 (.node(controlled_buffer_9_out));
  Pull_Resistor pull_resistor_9 (.node(controlled_buffer_10_out));
  Pull_Resistor pull_resistor_10 (.node(controlled_buffer_11_out));
  Pull_Resistor pull_resistor_11 (.node(controlled_buffer_12_out));
  Pull_Resistor pull_resistor_12 (.node(controlled_buffer_13_out));
  Pull_Resistor pull_resistor_13 (.node(controlled_buffer_14_out));
  Pull_Resistor pull_resistor_14 (.node(controlled_buffer_15_out));
  Pull_Resistor pull_resistor_15 (.node(controlled_buffer_16_out));
  Pull_Resistor pull_resistor_16 (.node(controlled_buffer_17_out));
  or or_1 (PCLOADOUT, controlled_buffer_2_out, controlled_buffer_3_out, controlled_buffer_4_out, controlled_buffer_5_out, controlled_buffer_6_out, controlled_buffer_7_out, controlled_buffer_8_out, controlled_buffer_9_out, controlled_buffer_10_out, controlled_buffer_11_out, controlled_buffer_12_out, controlled_buffer_13_out, controlled_buffer_14_out, controlled_buffer_15_out, controlled_buffer_16_out, controlled_buffer_17_out);

  // Notes on the sheet:
  //   1 = JMZ
  //   2 = JNZ
  //   3 = JLT
  //   4 = JNLT
  //   5 = JEQ
  //   7 = JGT
  //   8 = JNGT
  //   9 = JMS
  //   11 = JMC
  //   12 = JNC
  //   13 = JMB
  //   14 = JNB
  //   0 = JMP
  //   6 = JNEQ
  //   10 = JNS
endmodule

module STATUS (
  input  RESET,
  input  [7:0] STATUSIN,
  input  [7:0] STATUS32IN,
  input  ALUINEN,
  input  ALU32INEN,
  input  CLKIN,
  output [13:0] STATUSOUT
);

  wire or_2_out;
  wire [7:0] or_1_out;

  Pull_Resistor pull_resistor_1 (.node(STATUSIN));
  Pull_Resistor pull_resistor_2 (.node(STATUS32IN));
  assign or_1_out = STATUSIN | STATUS32IN;  // OR_Gate or_1, 8 bits wide
  or or_2 (or_2_out, ALUINEN, ALU32INEN);
  D_Flip_Flop CARRY (
    .clk(CLKIN), .D(or_1_out[0]), .Q(STATUSOUT[10]), .Qn(STATUSOUT[11]), .en(or_2_out), .reset(RESET));  // open: preset
  D_Flip_Flop BORROW (
    .clk(CLKIN), .D(or_1_out[1]), .Q(STATUSOUT[12]), .Qn(STATUSOUT[13]), .en(or_2_out), .reset(RESET));  // open: preset
  D_Flip_Flop SIGN (
    .clk(CLKIN), .D(or_1_out[2]), .Q(STATUSOUT[8]), .Qn(STATUSOUT[9]), .en(or_2_out), .reset(RESET));  // open: preset
  D_Flip_Flop ZERO (
    .clk(CLKIN), .D(or_1_out[3]), .Q(STATUSOUT[0]), .Qn(STATUSOUT[1]), .en(or_2_out), .reset(RESET));  // open: preset
  D_Flip_Flop GREATER_THAN (
    .clk(CLKIN), .D(or_1_out[4]), .Q(STATUSOUT[6]), .Qn(STATUSOUT[7]), .en(or_2_out), .reset(RESET));  // open: preset
  D_Flip_Flop EQUAL (
    .clk(CLKIN), .D(or_1_out[5]), .Q(STATUSOUT[4]), .Qn(STATUSOUT[5]), .en(or_2_out), .reset(RESET));  // open: preset
  D_Flip_Flop LESS_THAN (
    .clk(CLKIN), .D(or_1_out[6]), .Q(STATUSOUT[2]), .Qn(STATUSOUT[3]), .en(or_2_out), .reset(RESET));  // open: preset
  D_Flip_Flop d_ff_1 (.clk(CLKIN), .D(or_1_out[7]), .en(or_2_out), .reset(RESET));  // open: Q, Qn, preset
endmodule

module PAGE (
  input  PAGEOUT,
  input  [15:0] PAGEIN,
  input  PAGELOAD,
  input  RESET,
  input  CLKIN,
  output [15:0] PAGEMOVEOUT,
  output [15:0] PAGEOUT_2
);

  assign PAGEMOVEOUT = PAGEOUT ? PAGEOUT_2 : 16'bz;  // Controlled_Buffer controlled_buffer_1
  Register #(.width(16)) PAGE (.D(PAGEIN), .en(PAGELOAD), .Q(PAGEOUT_2), .clk(CLKIN), .clr(RESET));
endmodule

module TERMINAL (
  input  [15:0] RAMADDRIN,
  input  [15:0] RAMDATAIN,
  input  [15:0] RAMPAGEIN,
  input  RESET,
  input  RAMLOAD,
  input  RAMSTORE,
  input  RAMCLKIN,
  output [6:0] ASCIIOUT,
  output CLKOUT,
  output [15:0] RAMDATAOUT,
  output ENOUT,
  output CLEAROUT
);

  wire and_2_out, and_3_out, comparator_1_eq, comparator_2_eq, comparator_3_eq;

  Comparator #(.width(16)) comparator_1 (.a(RAMADDRIN), .b({16{1'b0}}), .eq(comparator_1_eq));  // open: gt, lt
  Comparator #(.width(16)) comparator_2 (.a(RAMADDRIN), .b(16'h1), .eq(comparator_2_eq));  // open: gt, lt
  Bit_Extender #(.in_width(16), .out_width(7)) bit_extender_1 (.in(RAMDATAIN), .out(ASCIIOUT));
  Comparator #(.width(16)) comparator_3 (.a(RAMPAGEIN), .b(16'ha), .eq(comparator_3_eq));  // open: gt, lt
  and and_1 (ENOUT, comparator_1_eq, comparator_3_eq, RAMSTORE);
  or or_1 (CLEAROUT, and_2_out, RESET);
  and and_2 (and_2_out, comparator_3_eq, comparator_2_eq, RAMCLKIN, RAMSTORE);
  assign RAMDATAOUT = and_3_out ? {16{1'b0}} : 16'bz;  // Controlled_Buffer controlled_buffer_1
  and and_3 (and_3_out, comparator_3_eq, RAMLOAD);

  assign CLKOUT = RAMCLKIN;
endmodule

module DATA (
  input  [15:0] RAMADDRIN,
  input  RAMLOAD,
  input  [15:0] RAMPAGEIN,
  output [15:0] RAMDATAOUT
);

  wire comparator_1_eq;
  wire [15:0] rom_1_data;

  Comparator #(.width(16)) comparator_1 (.a(RAMPAGEIN), .b(16'hb), .eq(comparator_1_eq));  // open: gt, lt
  ROM_part #(.addrWidth(16), .dataWidth(16)) rom_1 (.addr(RAMADDRIN), .data(rom_1_data), .sel(comparator_1_eq));
  assign RAMDATAOUT = RAMLOAD ? rom_1_data : 16'bz;  // Controlled_Buffer controlled_buffer_1

  // Notes on the sheet:
  //   contents of rom_1 (hex, n*v repeats v):
  //   68 65 6c 70 a 70 73 a 6c 73 20 2f a 63 61 74 20 2f 65 74 63 2f 70 61 73 73 77 64 a 65 63 68 6f 20
  //   30*3d a 65 63 68 6f 20 20 20 52 49 53 4b 59 20 4f 53 20 76 33 20 44 65 6d 6f a 65 63 68 6f 20 30*3d
  //   a 65 63 68 6f a 65 63 68 6f 20 2d 2d 2d 20 43 72 65 61 74 69 6e 67 20 66 69 6c 65 73 20 2d 2d 2d a
  //   6d 6b 66 69 6c 65 20 2f 68 65 6c 6c 6f a 77 72 69 74 65 20 2f 68 65 6c 6c 6f 20 48 65 6c 6c 6f 20 66
  //   72 6f 6d 20 52 49 53 4b 59 20 4f 53 20 76 33 21 a 63 61 74 20 2f 68 65 6c 6c 6f a 65 63 68 6f a 65
  //   63 68 6f 20 2d 2d 2d 20 4e 65 73 74 65 64 20 64 69 72 65 63 74 6f 72 69 65 73 20 2d 2d 2d a 6d 6b 64
  //   69 72 20 2f 6c 6f 67 73 a 6d 6b 66 69 6c 65 20 2f 6c 6f 67 73 2f 62 6f 6f 74 a 77 72 69 74 65 20 2f
  //   6c 6f 67 73 2f 62 6f 6f 74 20 53 79 73 74 65 6d 20 62 6f 6f 74 65 64 20 73 75 63 63 65 73 73 66 75
  //   6c 6c 79 a 63 61 74 20 2f 6c 6f 67 73 2f 62 6f 6f 74 a 65 63 68 6f a 65 63 68 6f 20 2d 2d 2d 20 44
  //   69 72 65 63 74 6f 72 79 20 6c 69 73 74 69 6e 67 73 20 2d 2d 2d a 6c 73 20 2f a 6c 73 20 2f 6c 6f 67
  //   73 a 65 63 68 6f a 65 63 68 6f 20 2d 2d 2d 20 50 72 6f 63 65 73 73 20 6c 69 73 74 69 6e 67 20 2d 2d
  //   2d a 70 73 a 65 63 68 6f a 65 63 68 6f 20 2d 2d 2d 20 50 69 70 65 73 20 2d 2d 2d a 70 69 70 65 a 65
  //   63 68 6f a 65 63 68 6f 20 44 6f 6e 65 2e 20 48 61 6c 74 69 6e 67 2e a 65 78 69 74 a
endmodule

module KBCTRL (
  input  [6:0] KBDAT,
  input  KBAV,
  input  [15:0] RAMPAGEIN,
  input  RESET,
  input  RAMLOAD,
  input  RAMCLKIN,
  output KBCLK,
  output KBAVAILABLE,
  output KBRD,
  output KBRST,
  output [15:0] RAMDATAOUT
);

  wire comparator_1_eq;
  wire [15:0] bit_extender_1_out;

  Comparator #(.width(16)) comparator_1 (.a(RAMPAGEIN), .b(16'hc), .eq(comparator_1_eq));  // open: gt, lt
  assign bit_extender_1_out = {{9{1'b0}}, KBDAT};  // Bit_Extender bit_extender_1
  assign RAMDATAOUT = KBRD ? bit_extender_1_out : 16'bz;  // Controlled_Buffer controlled_buffer_1
  and and_1 (KBRD, comparator_1_eq, RAMLOAD);

  assign KBAVAILABLE = KBAV;
  assign KBCLK = RAMCLKIN;
  assign KBRST = RESET;
endmodule
